# Fritzing sketch Diagrama (saved by Fritzing 0.8.7b)
breadboards: 1

parts:
  U1 = ESP8266 ESP-01 Upgraded WiFi Module [part_number=ESP8266]
  Parte1 = Arduino Uno (Rev3)
  GY1 = MPU-6050 Board GY-521 [form="♀ (female)" package=THT]
  J1 = Piezo Speaker
  Parte2 = Adafruit Proto Shield R3 [part_number="Adafruit #2077"]
  U2 = ESP8266 ESP-01 Upgraded WiFi Module [part_number=ESP8266]
  R1 = Resistor [tolerance=±5% resistance=2.2k package="0603 [SMD]"]
  R2 = Resistor [tolerance=±5% resistance=1k package="0603 [SMD]"]
  J2 = Piezo Speaker
  LED1 = LED - 5mm [color="Red (633nm)" package="5 mm [THT]"]
  LED2 = LED - 5mm [color="Green (565nm)" package="5 mm [THT]"]
  R3 = Resistor [tolerance=±5% resistance=220 package=THT]
  GY2 = MPU-6050 Board GY-521 [form="♀ (female)" package=THT]
  LED3 = LED - 5mm [color="Red (633nm)" package="5 mm [THT]"]
  LED4 = LED - 5mm [color="Green (565nm)" package="5 mm [THT]"]
  R4 = Resistor [tolerance=±5% resistance=220 package=THT]
  R5 = Resistor [tolerance=±5% resistance=1k package="0603 [SMD]"]
  R6 = Resistor [tolerance=±5% resistance=2.2k package="0603 [SMD]"]

nets:
  N1: U1.RXD, R5.Pin_1
  VCC: U1.VCC, U1.CH_PD, Parte1.3V3, GY1.pin1
  GND: U1.GND, Parte1.GND, GY1.pin2, J1.pin1, R4.Pin_1, R6.Pin_1
  N2: U1.TXD, Parte1.D2
  N3: Parte1.A4/SDA, GY1.pin4
  N4: Parte1.A5/SCL, GY1.pin3
  N5: Parte1.D8, LED3.anode
  N6: Parte1.D9_PWM, LED4.anode
  N7: Parte1.D13/SCK, J1.pin2
  N8: Parte1.D3_PWM, R5.Pin_0
  GND_2: Parte2.GND, Parte2.N$64, Parte2.N$113, Parte2.N$139, U2.GND, R1.Pin_0, J2.pin1, R3.Pin_0, GY2.pin2
  3.3V: Parte2.3.3V, Parte2.P$5, Parte2.1, Parte2.N$47, Parte2.N$144, Parte2.N$175, U2.VCC, U2.CH_PD, GY2.pin1
  N9: Parte2.A4, Parte2.N$76, Parte2.N$77, GY2.pin4
  N10: Parte2.A5, Parte2.N$95, Parte2.N$96, GY2.pin3
  N11: Parte2.D2, Parte2.N$128, Parte2.N$174, U2.TXD
  N12: Parte2.D3, Parte2.N$110, R2.Pin_1
  N13: Parte2.D8, LED1.anode
  N14: Parte2.D9, LED2.anode
  N15: Parte2.D13, J2.pin2
  N16: Parte2.N$106, Parte2.N$163, U2.RXD, R1.Pin_1, R2.Pin_0
  N17: Parte2.N$112, GY2.pin5
  N18: Parte2.N$129, GY2.pin6
  N19: Parte2.N$140, U2.GPIO_2
  N20: Parte2.N$142, GY2.pin8
  N21: Parte2.N$143, U2.RST/GPIO_16
  N22: Parte2.N$161, GY2.pin7
  N23: Parte2.N$162, U2.GPIO_0
  N24: LED1.cathode, LED2.cathode, R3.Pin_1
  N25: LED3.cathode, LED4.cathode, R4.Pin_0

notes:
  MPU | Arduino
  VCC 3.3V
  GND GND
  SCL A5
  SDA A4
  ESP | Arduino
  TX 2
  RX 3
  VCC 3.3 V
  CH_PD 3.3 V
  GND GND
  Pin | Función
  2 RX
  3 TX
  8 Red LED
  9 Green LED
  13 Buzzer

custom parts:
  ESP8266 ESP-01 Upgraded WiFi Module: Upgraded Version ESP-01,all Flash are upgraded to 1M byte.Also support Cloud service remote transmission.
  MPU-6050 Board GY-521: Acelerometro y Giroscopio MPU-6050 Board GY-521
  Adafruit Proto Shield R3: This prototyping shield is the best out there (well, we think so, at least), and now is even better with Version R3 - updated for the most compatibility with just about all the Arduinos! It works with UNO, Mega, Leonardo, NG, Diecimila, Duemilanove, and compatible Arduinos. Yun's and Arduino Ethernets have a chunky Ethernet jack that gets in the way of stacking, you can use the stacking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
